# Fritzing sketch elektrische_schema (saved by Fritzing 0.9.3b)
breadboards: 1

parts:
  M1 = DC Motor
  M2 = DC Motor
  M4 = DC Motor
  IC1 = L293D [package=THT]
  M5 = fc-51 [package=THT]
  M6 = fc-51 [package=THT]
  S1 = Reed switch [package=THT]
  S2 = Reed switch [package=THT]
  M3 = DC Motor
  VCC1 = 4 x AAA Battery Mount
  R6 = Resistor [tolerance=±5% resistance=220 package=THT]
  Part1 = Arduino Uno (Rev3)
  HC-SR04_Sensor_1 = HC-SR04 Ultrasonic Distance Sensor
  U2 = NodeMCU V3.0

nets (from the breadboard view):
  N1: M1.pin_1, M4.pin_1, IC1.Out_2_(_Controlled_by_Enable_1_)
  N2: M1.pin_2, M4.pin_2, IC1.Out_1_(_Controlled_by_Enable_1_)
  N3: M2.pin_1, IC1.Out_4_(_Controlled_by_Enable_2_), M3.pin_1
  N4: M2.pin_2, IC1.Out_3_(_Controlled_by_Enable_2_), M3.pin_2
  N5: IC1.Enable_1, U2.D1
  N6: IC1.In_1, Part1.D5_PWM
  5V: IC1.0V, IC1.+V, M5.pin2, M6.pin2, S1.pin_2, Part1.5V, HC-SR04_Sensor_1.VCC
  N7: IC1.In_2, Part1.D4
  N8: IC1.+Vmotor, VCC1.+
  N9: IC1.Enable_2, U2.D2
  N10: IC1.In_3, Part1.D7
  N11: IC1.In_4, Part1.D6_PWM
  N12: M5.pin1, U2.D3
  GND: M5.pin3, M6.pin3, Part1.GND, HC-SR04_Sensor_1.GND
  N13: M6.pin1, U2.SD2
  N14: S1.pin_1, S2.pin_1, R6.Pin_0, U2.D4
  N15: HC-SR04_Sensor_1.TRIG, U2.D6
  N16: HC-SR04_Sensor_1.ECHO, U2.D5

custom parts:
  NodeMCU V3.0: NodeMcu V3 Lua WIFI Development Board
